# Fritzing sketch H2GrowFritzing (saved by Fritzing 1.0.4)
breadboards: 1

parts:
  A1 = Particle - Photon2
  SENS1 = SoilWatch 10
  OLED_I2C1 = OLED 128x64 I2C Monochrome Display
  M1 = BMP280  # not connected
  Relay1 = Relay - 6 pins [package="DIP (Dual Inline) [THT]"]
  R1 = Resistor [tolerance=±5% resistance=2.2 package="0805 [SMD]"]
  WATER_PUMP1 = water pump/motor  # not connected
  Grove1 = Grove Dust Sensor
  R2 = Resistor [tolerance=±5% resistance=220 package="0805 [SMD]"]
  Q1 = PNP-Transistor [package="TO92 [THT]"]

nets:
  VCC: A1.Pin_2, A1.Pin_31, Relay1.VCC, Grove1.VCC
  GND: A1.Pin_4, A1.Pin_30, OLED_I2C1.GND, Relay1.GND, R1.Pin_0, Grove1.GND, Q1.C
  N1: A1.Pin_5, SENS1.OUT
  N2: A1.Pin_6, Grove1.SIG
  N3: A1.Pin_9, Relay1.IN, R1.Pin_1, Q1.B
  N4: A1.Pin_17, OLED_I2C1.SDA
  N5: A1.Pin_18, OLED_I2C1.SCK
  VCC_2: A1.Pin_26, SENS1.VCC, OLED_I2C1.VDD, Relay1.COM, R2.Pin_0
  N6: R2.Pin_1, Q1.E

custom parts:
  Particle - Photon2: The Photon 2 is a microcontroller and Wi-Fi networking developed by particle. Features: 802.11a/b/g/n Wi-Fi, 2.4 GHz and 5 GHz Integrated PCB antenna Integrated U.FL connector for external antenna Integrated RF switch BLE 5 using same antenna as Wi-Fi Realtek RTL8721DM MCU ARM Cortex M33 CPU, 200 MHz 2048 KB (2 MB) user application maximum size 3072 KB (3 MB) of RAM available to user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
  SoilWatch 10: SoilWatch 10 - Capacitive soil moisture sensor
  BMP280: Temperature Humidity Barometric presure Sensor, I2C
  Relay - 6 pins: A DIP stand-in part for whatever IC you want. With 6 pins on a 900mil dual inline package (DIP) footprint.
  water pump/motor: WATER PUMP BY ARDUBLOCKTR
  Grove Dust Sensor: PPD42 Grove Dust Sensor
